# Fritzing sketch pcb normal (saved by Fritzing 0.9.3b)
circuit board: 20.5874cm x 11.5254cm
breadboards: 1

parts:
  WAITING = LED - 5mm [color="Red (633nm)" package="5 mm [THT]"]
  CORTE = LED - 5mm [color="Red (633nm)" package="5 mm [THT]"]
  FALLO = LED - 5mm [color="Red (633nm)" package="5 mm [THT]"]
  ENG_ON = LED - 5mm [color="Red (633nm)" package="5 mm [THT]"]
  FAN_ON = LED - 5mm [color="Red (633nm)" package="5 mm [THT]"]
  STARTING = LED - 5mm [color="Red (633nm)" package="5 mm [THT]"]
  TRANSFER = LED - 5mm [color="Red (633nm)" package="5 mm [THT]"]
  R1 = Resistor [tolerance=±5% resistance=220 package=THT]
  R2 = Resistor [tolerance=±5% resistance=220 package=THT]
  R3 = Resistor [tolerance=±5% resistance=220 package=THT]
  R4 = Resistor [tolerance=±5% resistance=220 package=THT]
  R5 = Resistor [tolerance=±5% resistance=220 package=THT]
  R6 = Resistor [tolerance=±5% resistance=220 package=THT]
  R7 = Resistor [tolerance=±5% resistance=220 package=THT]
  ATMega_328P = atmega328 [package=dip]
  releFan = 888H-1CC-F-C E [part_number="888H-1CC-F-C E"]
  releTransfer = 888H-1CC-F-C E [part_number="888H-1CC-F-C E"]
  releStarter = 888H-1CC-F-C E [part_number="888H-1CC-F-C E"]
  releContacto = 888H-1CC-F-C E [part_number="888H-1CC-F-C E"]
  D12 = Resistor [tolerance=±5% resistance=10k package=THT]
  D11 = Resistor [tolerance=±5% resistance=10k package=THT]
  D10 = Resistor [tolerance=±5% resistance=10k package=THT]
  D9 = Resistor [tolerance=±5% resistance=10k package=THT]
  A2 = Resistor [tolerance=±5% resistance=10k package=THT]
  A4 = Resistor [tolerance=±5% resistance=10k package=THT]
  A3 = Resistor [tolerance=±5% resistance=10k package=THT]
  A1 = Resistor [tolerance=±5% resistance=10k package=THT]
  D0 = Resistor [tolerance=±5% resistance=10k package=THT]
  D4 = Resistor [tolerance=±5% resistance=10k package=THT]
  D1 = Resistor [tolerance=±5% resistance=10k package=THT]
  D7 = Resistor [tolerance=±5% resistance=10k package=THT]
  D5 = Resistor [tolerance=±5% resistance=10k package=THT]
  D6 = Resistor [tolerance=±5% resistance=10k package=THT]
  D8 = Resistor [tolerance=±5% resistance=10k package=THT]
  D13 = Resistor [tolerance=±5% resistance=10k package=THT]
  A0 = Resistor [tolerance=±5% resistance=10k package=THT]
  A5 = Resistor [tolerance=±5% resistance=10k package=THT]
  D2 = Resistor [tolerance=±5% resistance=10k package=THT]
  D3 = Resistor [tolerance=±5% resistance=10k package=THT]
  Servo = Camdenboss CTB0158-3 [part_number=CTB0158-3 package=THT]
  Ventilador = Camdenboss CTB0158-2 [part_number=CTB0158-2 package=THT]
  Contacto_+_Starter = Camdenboss CTB0158-4 [part_number=CTB0158-4 package=THT]
  Transfer = Camdenboss CTB0158-2 [part_number=CTB0158-2 package=THT]
  Alimentación = Camdenboss CTB0158-2 [part_number=CTB0158-2 package=THT]
  Componente2 = LCD1602-I2C
  diode1 = Rectifier Diode [part_number=1N4001 package="300 mil [THT]"]
  diode2 = Rectifier Diode [part_number=1N4001 package="300 mil [THT]"]
  diode3 = Rectifier Diode [part_number=1N4001 package="300 mil [THT]"]
  diode4 = Rectifier Diode [part_number=1N4001 package="300 mil [THT]"]
  Pad1 = Pad [width=7.902222222222222 height=9.0311111111111106 connect=center]
  Pad2 = Pad [width=7.902222222222222 height=9.0311111111111106 connect=center]
  Pad3 = Pad [width=7.902222222222222 height=9.0311111111111106 connect=center]
  Pad4 = Pad [width=7.902222222222222 height=9.0311111111111106 connect=center]
  RESET = Pushbutton [package="[THT]"]
  100nF = Ceramic Capacitor [capacitance=100nF package="100 mil [THT, multilayer]"]
  100nF_2 = Ceramic Capacitor [capacitance=100nF package="100 mil [THT, multilayer]"]
  10uF = Electrolytic Capacitor [capacitance=10µF package="100 mil [THT, electrolytic]"]
  100uF = Electrolytic Capacitor [capacitance=1µF voltage=16V package="200 mil [THT, electrolytic]"]
  RESET_10k = Resistor [tolerance=±5% resistance=10k package=THT]
  Pad5 = Pad [width=7.902222222222222 height=9.0311111111111106 connect=center]
  SPEAKER = Piezo Speaker
  10k = Resistor [tolerance=±5% resistance=10k package=THT]
  22k = Resistor [tolerance=±5% resistance=22k package=THT]
  Sensor_voltaje = Camdenboss CTB0158-2 [part_number=CTB0158-2 package=THT]
  Sensor_corte = Camdenboss CTB0158-3 [part_number=CTB0158-3 package=THT]
  MCP9701_TEMP = NPN-Transistor [package="TO92 [THT]"]
  MCP9701_AUX = NPN-Transistor [package="TO92 [THT]"]

nets:
  N1: WAITING.cathode, CORTE.cathode, FALLO.cathode, ENG_ON.cathode, FAN_ON.cathode, STARTING.cathode, TRANSFER.cathode, ATMega_328P.GND#7, releFan.1_+, releTransfer.1_+, releStarter.1_+, releContacto.1_+, D12.Pin_1, D11.Pin_1, D10.Pin_1, D9.Pin_1, A2.Pin_1, A4.Pin_1, A3.Pin_1, A1.Pin_1, D0.Pin_0, D4.Pin_0, D1.Pin_0, D7.Pin_0, D5.Pin_0, D6.Pin_0, D8.Pin_0, D13.Pin_1, A0.Pin_1, A5.Pin_1, D2.Pin_0, D3.Pin_0, Servo.pin3, Alimentación.pin2, Componente2.GND, diode1.anode, diode2.anode, diode3.anode, diode4.anode, Pad1.pad, Pad2.pad, Pad3.pad, Pad4.pad, RESET.Pin_3, RESET.Pin_4, 100nF.0, 10uF.-, 100uF.-, Pad5.pad, SPEAKER.pin2, 10k.Pin_1, Sensor_voltaje.pin1, Sensor_corte.pin1, MCP9701_TEMP.E, MCP9701_AUX.E
  N2: WAITING.anode, R1.Pin_0
  N3: CORTE.anode, R2.Pin_0
  N4: FALLO.anode, R7.Pin_0
  N5: ENG_ON.anode, R4.Pin_0
  N6: FAN_ON.anode, R5.Pin_0
  N7: STARTING.anode, R3.Pin_0
  N8: TRANSFER.anode, R6.Pin_0
  N9: R1.Pin_1, ATMega_328P.D6_(PWM), D6.Pin_1
  N10: R2.Pin_1, ATMega_328P.D2, D2.Pin_1
  N11: R3.Pin_1, ATMega_328P.D4, D4.Pin_1
  N12: R4.Pin_1, ATMega_328P.D3_(PWM), D3.Pin_1
  N13: R5.Pin_1, ATMega_328P.D5_(PWM), D5.Pin_1
  N14: R6.Pin_1, ATMega_328P.D7, D7.Pin_1
  N15: R7.Pin_1, ATMega_328P.D1_(TX), D1.Pin_1
  N16: ATMega_328P.RESET, RESET.Pin_1, RESET.Pin_2, RESET_10k.Pin_0
  N17: ATMega_328P.D0_(RX), D0.Pin_1, SPEAKER.pin1
  VCC: ATMega_328P.VCC, Componente2.VCC, 100nF.1, 10uF.+, RESET_10k.Pin_1, Sensor_corte.pin3, MCP9701_TEMP.B, MCP9701_AUX.B
  N18: ATMega_328P.D8, releContacto.22_-, D8.Pin_1, diode1.cathode
  N19: ATMega_328P.D9_(PWM), D9.Pin_0, Servo.pin1
  N20: ATMega_328P.D10_(PWM), releFan.22_-, D10.Pin_0, diode4.cathode
  N21: ATMega_328P.D11_(PWM), releTransfer.22_-, D11.Pin_0, diode3.cathode
  N22: ATMega_328P.D12, releStarter.22_-, D12.Pin_0, diode2.cathode
  N23: ATMega_328P.D13, D13.Pin_0, Sensor_corte.pin2
  N24: ATMega_328P.AVCC, 100nF_2.1
  N25: ATMega_328P.GND#21, 100nF_2.0
  N26: ATMega_328P.A0, A0.Pin_0, 10k.Pin_0, 22k.Pin_1
  N27: ATMega_328P.A1, A1.Pin_0, MCP9701_TEMP.C
  N28: ATMega_328P.A2, A2.Pin_0, MCP9701_AUX.C
  N29: ATMega_328P.A3, A3.Pin_0
  N30: ATMega_328P.A4, A4.Pin_0, Componente2.SDA
  N31: ATMega_328P.A5, A5.Pin_0, Componente2.SCL
  N32: releFan.11_N.O., Ventilador.pin1
  N33: releFan.9_COM, Ventilador.pin2
  N34: releTransfer.11_N.O., Transfer.pin1
  N35: releTransfer.9_COM, Transfer.pin2
  N36: releStarter.11_N.O., Contacto_+_Starter.pin3
  N37: releStarter.9_COM, Contacto_+_Starter.pin4
  N38: releContacto.11_N.O., Contacto_+_Starter.pin1
  N39: releContacto.9_COM, Contacto_+_Starter.pin2
  N40: Servo.pin2, Alimentación.pin1, 100uF.+
  N41: 22k.Pin_0, Sensor_voltaje.pin2

notes:
  pull-down
  Fuente 5V
  Sensor RPM
  Sensor TEMP
  TO-DO:
  GND
  WayWayWay

custom parts:
  LCD1602-I2C: A standard character display, usually with 2x16 characters. Comes in many colors with LCM1602 IIC attached.
